# Fritzing sketch Diagrama (saved by Fritzing 0.9.3b)
breadboards: 2

parts:
  Componente1 = Arduino Mega ADK (Rev3)
  Disp2 = LBT2088AH [part_number=LBT2088AH]
  S1 = Pushbutton [package="[THT]"]
  S2 = Pushbutton [package="[THT]"]
  S3 = Pushbutton [package="[THT]"]
  S4 = Pushbutton [package="[THT]"]
  S5 = Pushbutton [package="[THT]"]
  R2 = Resistor [tolerance=±5% resistance=330 package=THT]
  R3 = Resistor [tolerance=±5% resistance=330 package=THT]
  R4 = Resistor [tolerance=±5% resistance=330 package=THT]
  R5 = Resistor [tolerance=±5% resistance=330 package=THT]
  R6 = Resistor [tolerance=±5% resistance=330 package=THT]
  S6 = Pushbutton [package="[THT]"]
  S7 = Pushbutton [package="[THT]"]
  S8 = Pushbutton [package="[THT]"]
  R7 = Resistor [tolerance=±5% resistance=330 package=THT]
  R8 = Resistor [tolerance=±5% resistance=330 package=THT]
  R9 = Resistor [tolerance=±5% resistance=330 package=THT]
  Disp1 = LBT2088AH [part_number=LBT2088AH]
  U1 = MAX7219 [package=dil24]

nets:
  N1: Componente1.D21/SCL, S7.Pin_3, S7.Pin_4, R9.Pin_1
  N2: Componente1.D20/SDA, Componente1.D19/RX1, S5.Pin_3, S5.Pin_4, R2.Pin_1
  N3: Componente1.D17/RX2, Disp2.pin_8
  N4: Componente1.D16/TX2, Disp2.pin_7
  N5: Componente1.D15/RX3, Disp2.pin_6
  N6: Componente1.D14/TX3, Disp2.pin_5
  N7: Componente1.D13_PWM, Disp2.pin_4
  N8: Componente1.D12_PWM, Disp2.pin_3
  N9: Componente1.D11_PWM, Disp2.pin2
  N10: Componente1.D10_PWM, Disp2.pin1
  N11: Componente1.D9_PWM, Disp2.pin_9
  N12: Componente1.D8_PWM, Disp2.pin_10
  5V: Componente1.5V, R2.Pin_0, R3.Pin_0, R4.Pin_0, R5.Pin_0, R6.Pin_0, R7.Pin_0, R8.Pin_0, R9.Pin_0, U1.VCC
  GND: Componente1.GND, S1.Pin_1, S1.Pin_2, S2.Pin_1, S2.Pin_2, S3.Pin_1, S3.Pin_2, S4.Pin_1, S4.Pin_2, S5.Pin_1, S5.Pin_2, S6.Pin_1, S6.Pin_2, S7.Pin_1, S7.Pin_2, S8.Pin_1, S8.Pin_2, U1.GND
  N13: Componente1.D2_PWM, Disp2.pin_16
  N14: Componente1.D3_PWM, Disp2.pin_15
  N15: Componente1.D4_PWM, Disp2.pin_14
  N16: Componente1.D5_PWM, Disp2.pin_13
  N17: Componente1.D6_PWM, Disp2.pin_12
  N18: Componente1.D7_PWM, Disp2.pin_11
  N19: Componente1.D22, S2.Pin_3, S2.Pin_4, R3.Pin_1
  N20: Componente1.D23, S1.Pin_3, S1.Pin_4, R6.Pin_1
  N21: Componente1.D24, S3.Pin_3, S3.Pin_4, R5.Pin_1
  N22: Componente1.D25, S4.Pin_3, S4.Pin_4, R4.Pin_1
  N23: Componente1.D31, S8.Pin_3, S8.Pin_4, R8.Pin_1
  N24: Componente1.D33, S6.Pin_3, S6.Pin_4, R7.Pin_1
  N25: Componente1.D51/MOSI, U1.DIN
  N26: Componente1.D52/SCK, U1.CLK
  N27: Componente1.D53/SS, U1.LOAD
  N28: Disp1.pin1, U1.DIG0
  N29: Disp1.pin2, U1.DIG1
  N30: Disp1.pin_3, U1.DIG2
  N31: Disp1.pin_4, U1.DIG3
  N32: Disp1.pin_5, U1.DIG4
  N33: Disp1.pin_6, U1.DIG5
  N34: Disp1.pin_7, U1.DIG6
  N35: Disp1.pin_8, U1.DIG7
  N36: Disp1.pin_9, U1.SEGG
  N37: Disp1.pin_10, U1.SEGF
  N38: Disp1.pin_11, U1.SEGE
  N39: Disp1.pin_12, U1.SEGD
  N40: Disp1.pin_13, U1.SEGC
  N41: Disp1.pin_14, U1.SEGB
  N42: Disp1.pin_15, U1.SEGA
  N43: Disp1.pin_16, U1.SEGDP
